// Logisim project Q0translogic.circ as structural Verilog
module Q0transition (
  input  D2,
  input  D1,
  input  D0,
  output Q0
);

  wire and_1_out, not_1_out, not_2_out;

  not not_1 (not_1_out, D2);
  not not_2 (not_2_out, D0);
  and and_1 (and_1_out, not_1_out, D1);
  or or_1 (Q0, not_2_out, and_1_out);
endmodule
