// Logisim project Q1translogic.circ as structural Verilog
module Q1transition (
  input  D2,
  input  D1,
  input  D0,
  output Q1
);

  wire and_1_out, not_1_out, not_2_out;

  not not_1 (not_1_out, D0);
  not not_2 (not_2_out, D2);
  and and_1 (and_1_out, D1, not_1_out);
  or or_1 (Q1, not_2_out, and_1_out);
endmodule
