// Logisim project Q2translogic.circ as structural Verilog
module Q2transition (
  input  D2,
  input  D1,
  input  D0,
  output Q2
);


  assign Q2 = D0;
endmodule
